# Fritzing sketch blinds (saved by Fritzing 0.9.4)
breadboards: 1

parts:
  Wemos_D1_mini = WeMos D1 Mini
  Hanpose_17HS3401S = Stepper Motor - Bipolar
  BigTreeTech_v3 = SilentStepStick TMC2130 [package=SO16]
  C1 = Ceramic Capacitor [capacitance=100nF package="100 mil [THT, multilayer]"]
  C2 = Electrolytic Capacitor [capacitance=100μF package="0807 [SMD, electrolytic]"]
  V1 = DC Power [voltage=12V]

nets:
  N1: Wemos_D1_mini.5V, BigTreeTech_v3.VIO
  N2: Wemos_D1_mini.D7, BigTreeTech_v3.STEP
  N3: Wemos_D1_mini.D8, BigTreeTech_v3.DIR
  N4: Wemos_D1_mini.G, BigTreeTech_v3.GND#8
  N5: Hanpose_17HS3401S.A, BigTreeTech_v3.2B
  N6: Hanpose_17HS3401S.C, BigTreeTech_v3.2A
  N7: Hanpose_17HS3401S.B, BigTreeTech_v3.1A
  N8: Hanpose_17HS3401S.D, BigTreeTech_v3.1B
  N9: BigTreeTech_v3.GND#14, C1.1, C2.-, V1.V-
  N10: BigTreeTech_v3.VMOT, C1.0, C2.+, V1.V+

custom parts:
  WeMos D1 Mini: The D1 mini is a mini wifi board based on ESP-8266EX.
  SilentStepStick TMC2130: The TMC2130 provides an integrated motor driver solution for 3D-Printing, Cameras, Scanners and other automated equipment applications. The device has an integrated microstepping indexer, the sensorless stall detection technology StallGuard2™, the sensorless load dependent current control CoolStep™ and the completely noiseless current control mode StealthChop™ and is intended to drive a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
