# Fritzing sketch psu (saved by Fritzing 0.9.4)
breadboards: 1

parts:
  CONN1 = USB connector [package=THT]
  CONN2 = USB connector [package=THT]
  CONN3 = USB connector [package=THT]
  CONN4 = USB connector [package=THT]
  F1 = Resettable Fuse PTC [package=ptc]
  F2 = Resettable Fuse PTC [package=ptc]
  F3 = Resettable Fuse PTC [package=ptc]
  F4 = Resettable Fuse PTC [package=ptc]
  DC1 = DC_DC_XL4016 [package=board_screw]
  V1 = DC Power [voltage=19]

nets:
  N1: CONN1.5V, F1.1
  N2: CONN1.d-, CONN1.d+
  N3: CONN1.chassis5, CONN1.chassis6, CONN2.chassis5, CONN2.chassis6
  N4: CONN2.5V, F2.1
  N5: CONN2.d-, CONN2.d+
  N6: CONN3.5V, F3.1
  N7: CONN3.d-, CONN3.d+
  N8: CONN3.chassis5, CONN4.chassis5, DC1.OUT-
  N9: CONN4.5V, F4.1
  N10: CONN4.d-, CONN4.d+
  N11: F1.2, F2.2, F3.2, F4.2, DC1.OUT+
  N12: DC1.IN+, V1.V+
  N13: DC1.IN-, V1.V-
