# Fritzing sketch stove (saved by Fritzing 0.9.4)
breadboards: 1

parts:
  WeMos_D1_Mini1 = WeMos D1 Mini
  U1 = 3.5mm Audio Jack [package=audio-jack]
  R1 = Resistor [tolerance=±1% resistance=470k package=THT]
  R2 = Resistor [tolerance=±1% resistance=470k package=THT]
  Burden = Resistor [tolerance=±1% resistance=22 package=THT]

nets:
  N1: WeMos_D1_Mini1.3V3, R2.Pin_1
  N2: WeMos_D1_Mini1.A0, U1.SLEEVE, Burden.Pin_1
  N3: WeMos_D1_Mini1.G, R1.Pin_1
  N4: U1.LEFT, R1.Pin_0, R2.Pin_0, Burden.Pin_0

custom parts:
  WeMos D1 Mini: The D1 mini is a mini wifi board based on ESP-8266EX.
