# Fritzing sketch tv_remote (saved by Fritzing 0.9.4)
breadboards: 1

parts:
  WeMos_D1_Mini1 = WeMos D1 Mini
  LED1 = LED - 5mm [color="Infrared (940nm)" current=0.1A package="5 mm [THT]"]
  U1 = 3.5mm Audio Jack [package=audio-jack]
  R1 = Resistor [tolerance=±1% resistance=100 package=THT]
  R2 = Resistor [tolerance=±1% resistance=470k package=THT]
  R3 = Resistor [tolerance=±1% resistance=470k package=THT]

nets:
  N1: WeMos_D1_Mini1.3V3, R1.Pin_1
  N2: WeMos_D1_Mini1.5V, R3.Pin_1
  N3: WeMos_D1_Mini1.A0, U1.SLEEVE
  N4: WeMos_D1_Mini1.D7, LED1.anode
  N5: WeMos_D1_Mini1.G, R2.Pin_1
  N6: LED1.cathode, R1.Pin_0
  N7: U1.LEFT, R2.Pin_0, R3.Pin_0

custom parts:
  WeMos D1 Mini: The D1 mini is a mini wifi board based on ESP-8266EX.
